# Fritzing sketch knockbox_atmega168 (saved by Fritzing 0.9.2b)
circuit board: 8.46667cm x 5.64444cm
stripboards: 1

parts:
  R1 = Resistor [tolerance=±5% resistance=220 package=THT]
  R2 = Resistor [tolerance=±5% resistance=220 package=THT]
  Red_LED = female pin header, 2 pins [form="♀ (female)"]
  Blue_LED = female pin header, 2 pins [form="♀ (female)"]
  Servo = male pin header, 3 pins [form="♂ (male)"]
  R3 = Resistor [tolerance=±5% resistance=1M package=THT]
  V1 = DC Power [voltage=5V]
  U1 = atmega168 [package=dip]
  Switch = female pin header, 2 pins [form="♀ (female)"]
  LED_Strip = male pin header, 3 pins [form="♂ (male)"]
  Piezo = female pin header, 2 pins [form="♀ (female)"]

nets:
  N1: R1.Pin_0, U1.D2
  N2: R1.Pin_1, Red_LED.pin2
  N3: R2.Pin_0, U1.D3_(PWM)
  N4: R2.Pin_1, Blue_LED.pin1
  N5: Red_LED.pin1, Blue_LED.pin2, Servo.pin3, R3.Pin_1, V1.V-, U1.GND, Switch.pin2, LED_Strip.pin1, Piezo.pin1
  N6: Servo.pin1, U1.D8
  N7: Servo.pin2, V1.V+, U1.VCC, U1.AVCC, U1.AREF, LED_Strip.pin2
  N8: R3.Pin_0, U1.A0, Piezo.pin2
  N9: U1.D4, LED_Strip.pin3
  N10: U1.D7, Switch.pin1
